# Fritzing sketch FightersoftheForumBreadboard.CircuitDiagram (saved by Fritzing 0.8.7b)
breadboards: 1

parts:
  Raspberry_Pi_B_rev2 = Raspberry Pi B rev1
  North = Pushbutton [package="[THT]"]
  S1 = Pushbutton [package="[THT]"]
  S2 = Pushbutton [package="[THT]"]
  S3 = Pushbutton [package="[THT]"]
  S4 = Pushbutton [package="[THT]"]
  S5 = Pushbutton [package="[THT]"]
  S6 = Pushbutton [package="[THT]"]
  R1 = Resistor [tolerance=±5% resistance=220 package=THT]
  LED1 = LED - 5mm [color="Red (633nm)" package="5 mm [THT]"]
  LED3 = smd LED [color="Blue (430nm)" package="0805 [SMD]"]
  LED4 = smd LED [color="Yellow (585nm)" package="0805 [SMD]"]
  R2 = Resistor [tolerance=±5% resistance=220 package=THT]
  R3 = Resistor [tolerance=±5% resistance=220 package=THT]

nets:
  N1: Raspberry_Pi_B_rev2.GPIO_0, LED1.cathode
  N2: Raspberry_Pi_B_rev2.GPIO_1, LED4.cathode
  N3: Raspberry_Pi_B_rev2.GND, North.Pin_1, North.Pin_2, S1.Pin_1, S1.Pin_2, S2.Pin_1, S2.Pin_2, S3.Pin_1, S3.Pin_2, R1.Pin_1, R2.Pin_1, R3.Pin_1
  N4: Raspberry_Pi_B_rev2.GPIO_23, S3.Pin_3, S3.Pin_4
  N5: Raspberry_Pi_B_rev2.GPIO_14, S6.Pin_3, S6.Pin_4
  N6: Raspberry_Pi_B_rev2.GPIO_15, S5.Pin_3, S5.Pin_4
  N7: Raspberry_Pi_B_rev2.GPIO_17, S4.Pin_3, S4.Pin_4
  N8: Raspberry_Pi_B_rev2.GPIO_18, North.Pin_3, North.Pin_4
  N9: Raspberry_Pi_B_rev2.GPIO_21, S1.Pin_3, S1.Pin_4
  N10: Raspberry_Pi_B_rev2.GPIO_22, S2.Pin_3, S2.Pin_4
  N11: Raspberry_Pi_B_rev2.GPIO_4, LED3.cathode
  N12: Raspberry_Pi_B_rev2.5V, S4.Pin_1, S4.Pin_2, S5.Pin_1, S5.Pin_2, S6.Pin_1, S6.Pin_2
  N13: R1.Pin_0, LED4.anode
  N14: LED1.anode, R3.Pin_0
  N15: LED3.anode, R2.Pin_0
